# Fritzing sketch Crazy box Sketch (saved by Fritzing 0.9.0b)

parts:
  Part1 = Arduino Uno (Rev3)
  Part2 = LED Matrix - Serial Interface - Red/Green/Blue
  Part3 = Shift Register Breakout - 74HC595
  Part4 = Shift Register Breakout - 74HC595
  J1 = Basic Servo
  J2 = Basic Servo
  S1 = Square Pushbutton

nets:
  N1: Part1.D8, S1.leg1
  N2: Part1.D9_PWM, J2.pulse
  N3: Part1.D10_PWM/SS, J1.pulse
  N4: Part1.D11_PWM/MOSI, Part3.SERIAL_IN
  N5: Part1.D12/MISO, Part3.LATCH_CLOCK, Part4.LATCH_CLOCK
  N6: Part1.D13/SCK, Part3.CLOCK, Part4.CLOCK
  GND: Part1.GND, Part3.GND, Part4.GND, J1.gnd, J2.gnd, S1.leg0
  VCC: Part1.5V, Part3.VCC, Part4.VCC, J1.vcc, J2.vcc
  N7: Part2.VCC, Part3.QE, Part3.QF, Part4.QA, Part4.QB
  N8: Part2.SCK, Part3.QD, Part4.QC
  N9: Part2.CS, Part3.QC, Part4.QD
  N10: Part2.MISO, Part3.QB
  N11: Part2.GND, Part3.QA, Part4.QF
  N12: Part2.MOSI, Part4.QE
  N13: Part3.SERIAL_OUT, Part4.SERIAL_IN
